// Logisim project Locker.circ as structural Verilog: 17 circuits, main circuit TOP
module main (
  input  Reset,
  input  P0,
  input  P1,
  input  P2,
  input  P3,
  input  Enter,
  output [6:0] out_7,
  output [6:0] out_8,
  output [6:0] out_9,
  output [6:0] out_10,
  output [6:0] out_11,
  output [6:0] out_12,
  output [6:0] out_13,
  output [6:0] out_14,
  output [6:0] out_15,
  output [6:0] out_16,
  output [6:0] out_17,
  output [6:0] out_18,
  output [6:0] out_19,
  output [6:0] out_20,
  output [6:0] out_21,
  output [6:0] out_22,
  output [6:0] out_23,
  output [6:0] out_24,
  output [6:0] out_25,
  output [6:0] out_26,
  output [6:0] out_27,
  output [6:0] out_28,
  output [6:0] out_29,
  output [6:0] Flash,
  output [6:0] Flash_2,
  output out_32,
  output out_33,
  output [6:0] out_34,
  output [6:0] out_35
);

  wire Clean, Clock, Fail, keypad_encoder_1_key_pressed, Pass_Reset, Result, Set, Timer_Out, Timer_Reset,
       Times_Out, Times_Reset;
  wire [1:0] keypad_encoder_1_key_value;
  wire [2:0] Condition, Count;
  wire [7:0] Input, New_Pass, password_storage_1_current_password;

  // DipSwitch #(.NSwitches(8)) New_Password: pin names not known; wires that end beside it: New_Pass[0], New_Pass[1], New_Pass[2], New_Pass[3], New_Pass[4], New_Pass[5], New_Pass[6], New_Pass[7]
  Timer_Locker timer_locker_1 (.Input_Count(Count), .Time_Out(Timer_Out), .Clock(Clock), .Timer_Reset(Timer_Reset));
  Times_Locker times_locker_1 (.Fail(Fail), .Clock(Clock), .Time_Out(Times_Out), .Reset(Times_Reset));
  Button Password_Reset (.out(Pass_Reset));
  Button Set_Password (.out(Set));
  DIsplay_Driver display_driver_1 (
    .Count(Count), .Input(Input), .out_4(out_7), .out_5(out_8), .out_6(out_9), .out_7(out_10),
    .out_8(out_11), .out_9(out_12), .out_10(out_13), .out_11(out_14), .out_12(out_15), .out_13(out_16),
    .out_14(out_17), .out_15(out_18), .out_16(out_19), .out_17(out_20), .out_18(out_21), .out_19(out_22),
    .out_20(out_23), .out_21(out_24), .out_22(out_25), .out_23(out_26), .out_24(out_27), .out_25(out_28),
    .out_26(out_29), .Condition(Condition));
  DotMatrix #(.matrixcols(23)) dotmatrix_1 (
    .col0(out_7), .col1(out_8), .col2(out_9), .col3(out_10), .col4(out_11), .col5(out_12), .col6(out_13),
    .col7(out_14), .col8(out_15), .col9(out_16), .col10(out_17), .col11(out_18), .col12(out_19),
    .col13(out_20), .col14(out_21), .col15(out_22), .col16(out_23), .col17(out_24), .col18(out_25),
    .col19(out_26), .col20(out_27), .col21(out_28), .col22(out_29));
  Clock clock_1 (.out(Clock));
  Keypad_Encoder keypad_encoder_1 (
    .P0(P0), .P1(P1), .P2(P2), .P3(P3), .Key_Pressed(keypad_encoder_1_key_pressed),
    .Key_Value(keypad_encoder_1_key_value));
  not not_1 (Flash[3], Flash[6]);
  not not_2 (Flash[5], Flash[6]);
  Input_Capture input_capture_1 (
    .Load_Input(keypad_encoder_1_key_pressed), .Key_Value(keypad_encoder_1_key_value), .Clock(Clock),
    .Clean_Input(Clean), .Input_Sequence(Input), .Input_Count(Count));
  not not_3 (Flash[1], Flash[6]);
  Password_Storage password_storage_1 (
    .Clock(Clock), .New_Password(New_Pass), .Set_Password(Set),
    .Current_Password(password_storage_1_current_password), .Reset_Password(Pass_Reset));
  // Probe on password_storage_1_current_password
  // Probe on Input
  Password_Comparator password_comparator_1 (
    .Input_Sequence(Input), .Current_Password(password_storage_1_current_password), .Compare_Result(Result));
  Processor processor_1 (
    .Result(Result), .Count(Count), .Enter(Enter), .Set(Set), .Timer_out(Timer_Out), .Times_Out(Times_Out),
    .Reset(Reset), .Clock(Clock), .Fail(Fail), .Condition(Condition), .Clean(Clean), .Flash_Out(Flash[6]),
    .Timer_Reset(Timer_Reset), .Times_Reset(Times_Reset));

  assign {Flash[4], Flash[2], Flash[0]} = {3{Flash[6]}};
  assign Flash_2 = {Flash[6:5], Flash[6], Flash[3], Flash[6], Flash[1], Flash[6]};
  assign out_32 = Flash[3];
  assign out_33 = Flash[6];
  assign out_34 = out_12;
  assign out_35 = out_24;

  // Other names for the same wires on the sheet: Flash_t = Flash[6]

  // Notes on the sheet:
  //   超时与错误处理区
  //   密码设置区
  //   时钟
  //   显示区
  //   密码输入与处理区
  //   状态处理区
  //   正确密码
  //   当前输入
endmodule

module Keypad_Encoder (
  input  P0,
  input  P1,
  input  P2,
  input  P3,
  output Key_Pressed,
  output [1:0] Key_Value
);

  or or_1 (Key_Pressed, P0, P1, P2, P3);
  or or_2 (Key_Value[0], P1, P3);
  or or_3 (Key_Value[1], P2, P3);

  // Notes on the sheet:
  //   按钮编码
endmodule

module Input_Capture (
  input  Load_Input,
  input  [1:0] Key_Value,
  input  Clock,
  input  Clean_Input,
  output [7:0] Input_Sequence,
  output [2:0] Input_Count
);

  wire and_1_out, comparator_1_lt, demultiplexer_1_out0, demultiplexer_1_out1, demultiplexer_1_out2,
       demultiplexer_1_out3, not_1_out, register_1_q, register_2_q;
  wire [7:0] counter_1_q;

  and and_1 (and_1_out, register_1_q, ~register_2_q);  // AND_Gate
  Register #(.width(1), .Select("low")) register_1 (.D(Load_Input), .Q(register_1_q), .clk(Clock));  // open: en, clr
  Register #(.width(1), .Select("low")) register_2 (.D(register_1_q), .Q(register_2_q), .clk(Clock));  // open: en, clr
  Demultiplexer #(.select(2), .enable("false")) demultiplexer_1 (
    .out0(demultiplexer_1_out0), .out1(demultiplexer_1_out1), .out2(demultiplexer_1_out2),
    .out3(demultiplexer_1_out3), .in(and_1_out), .sel(counter_1_q[1:0]));
  Counter counter_1 (
    .count(and_1_out), .Q(counter_1_q), .clk(Clock), .clr(Clean_Input));  // open: load, D, carry, preset, down
  Register #(.width(2), .Select("low")) register_3 (
    .D(Key_Value), .en(demultiplexer_1_out0), .Q(Input_Sequence[1:0]), .clk(Clock), .clr(Clean_Input));
  Register #(.width(2), .Select("low")) register_4 (
    .D(Key_Value), .en(demultiplexer_1_out1), .Q(Input_Sequence[3:2]), .clk(Clock), .clr(Clean_Input));
  Register #(.width(2), .Select("low")) register_5 (
    .D(Key_Value), .en(demultiplexer_1_out2), .Q(Input_Sequence[5:4]), .clk(Clock), .clr(Clean_Input));
  Register #(.width(2), .Select("low")) register_6 (
    .D(Key_Value), .en(demultiplexer_1_out3), .Q(Input_Sequence[7:6]), .clk(Clock), .clr(Clean_Input));
  not not_1 (not_1_out, comparator_1_lt);
  Comparator comparator_1 (.a(counter_1_q), .b(8'h4), .lt(comparator_1_lt));  // open: gt, eq
  Multiplexer #(.width(3), .enable("false")) multiplexer_1 (
    .in0({1'b0, counter_1_q[1:0]}), .in1(3'b100), .out(Input_Count), .sel(not_1_out));

  // Notes on the sheet:
  //   捕获上升沿
  //   存储当前输入并计数
endmodule

module Password_Storage (
  input  Clock,
  input  [7:0] New_Password,
  input  Set_Password,
  input  Reset_Password,
  output [7:0] Current_Password
);

  wire or_1_out;
  wire [1:0] multiplexer_1_out, multiplexer_2_out, multiplexer_3_out, multiplexer_4_out;

  Multiplexer #(.width(2), .enable("false")) multiplexer_1 (
    .in0(New_Password[1:0]), .in1(2'b00), .out(multiplexer_1_out), .sel(Reset_Password));
  or or_1 (or_1_out, Set_Password, Reset_Password);
  Register #(.width(2), .Select("low")) register_1 (
    .D(multiplexer_1_out), .en(or_1_out), .Q(Current_Password[1:0]), .clk(Clock));  // open: clr
  Register #(.width(2), .Select("low")) register_2 (
    .D(multiplexer_2_out), .en(or_1_out), .Q(Current_Password[3:2]), .clk(Clock));  // open: clr
  Multiplexer #(.width(2), .enable("false")) multiplexer_2 (
    .in0(New_Password[3:2]), .in1(2'b01), .out(multiplexer_2_out), .sel(Reset_Password));
  Register #(.width(2), .Select("low")) register_3 (
    .D(multiplexer_3_out), .en(or_1_out), .Q(Current_Password[5:4]), .clk(Clock));  // open: clr
  Multiplexer #(.width(2), .enable("false")) multiplexer_3 (
    .in0(New_Password[5:4]), .in1(2'b10), .out(multiplexer_3_out), .sel(Reset_Password));
  Multiplexer #(.width(2), .enable("false")) multiplexer_4 (
    .in0(New_Password[7:6]), .in1(2'b11), .out(multiplexer_4_out), .sel(Reset_Password));
  Register #(.width(2), .Select("low")) register_4 (
    .D(multiplexer_4_out), .en(or_1_out), .Q(Current_Password[7:6]), .clk(Clock));  // open: clr

  // Notes on the sheet:
  //   存储当前密码 可重置和设置
endmodule

module Password_Comparator (
  input  [7:0] Input_Sequence,
  input  [7:0] Current_Password,
  output Compare_Result
);

  wire comparator_1_eq, comparator_2_eq, comparator_3_eq, comparator_4_eq;

  Comparator #(.width(2)) comparator_1 (
    .a(Input_Sequence[1:0]), .b(Current_Password[1:0]), .eq(comparator_1_eq));  // open: gt, lt
  Comparator #(.width(2)) comparator_2 (
    .a(Input_Sequence[3:2]), .b(Current_Password[3:2]), .eq(comparator_2_eq));  // open: gt, lt
  Comparator #(.width(2)) comparator_3 (
    .a(Input_Sequence[5:4]), .b(Current_Password[5:4]), .eq(comparator_3_eq));  // open: gt, lt
  Comparator #(.width(2)) comparator_4 (
    .a(Input_Sequence[7:6]), .b(Current_Password[7:6]), .eq(comparator_4_eq));  // open: gt, lt
  and and_1 (Compare_Result, comparator_1_eq, comparator_2_eq, comparator_3_eq, comparator_4_eq);

  // Notes on the sheet:
  //   密码比较器
endmodule

module DIsplay_Driver (
  input  [2:0] Count,
  input  [7:0] Input,
  input  [2:0] Condition,
  output [6:0] out_4,
  output [6:0] out_5,
  output [6:0] out_6,
  output [6:0] out_7,
  output [6:0] out_8,
  output [6:0] out_9,
  output [6:0] out_10,
  output [6:0] out_11,
  output [6:0] out_12,
  output [6:0] out_13,
  output [6:0] out_14,
  output [6:0] out_15,
  output [6:0] out_16,
  output [6:0] out_17,
  output [6:0] out_18,
  output [6:0] out_19,
  output [6:0] out_20,
  output [6:0] out_21,
  output [6:0] out_22,
  output [6:0] out_23,
  output [6:0] out_24,
  output [6:0] out_25,
  output [6:0] out_26
);

  wire decoder_1_out1, decoder_1_out2, decoder_1_out3, decoder_1_out4, or_1_out, or_2_out, or_3_out, or_4_out;
  wire [6:0] alpha_mapper_1_out_2, alpha_mapper_1_out_3, alpha_mapper_1_out_4, alpha_mapper_1_out_5,
       multiplexer_1_out, multiplexer_2_out, multiplexer_3_out, multiplexer_4_out, multiplexer_5_out,
       multiplexer_6_out, multiplexer_7_out, multiplexer_8_out, number_mapper_1_out_2, number_mapper_1_out_3,
       number_mapper_1_out_4, number_mapper_1_out_5;

  Decoder #(.select(3), .enable("false")) decoder_1 (
    .out1(decoder_1_out1), .out2(decoder_1_out2), .out3(decoder_1_out3), .out4(decoder_1_out4), .sel(Count));  // open: out0, out5, out6, out7
  Number_Mapper number_mapper_1 (
    .Input(Input), .out_2(number_mapper_1_out_2), .out_3(number_mapper_1_out_3),
    .out_4(number_mapper_1_out_4), .out_5(number_mapper_1_out_5));
  Alpha_Mapper alpha_mapper_1 (
    .Condition(Condition), .out_2(alpha_mapper_1_out_2), .out_3(alpha_mapper_1_out_3),
    .out_4(alpha_mapper_1_out_4), .out_5(alpha_mapper_1_out_5));
  or or_1 (or_1_out, decoder_1_out1, decoder_1_out2, decoder_1_out3, decoder_1_out4);
  or or_2 (or_2_out, decoder_1_out2, decoder_1_out3, decoder_1_out4);
  or or_3 (or_3_out, decoder_1_out3, decoder_1_out4);
  or or_4 (or_4_out, Condition[0], Condition[1], Condition[2]);
  Multiplexer #(.width(7), .enable("false")) multiplexer_1 (
    .in0(7'b0000101), .in1(number_mapper_1_out_2), .out(multiplexer_1_out), .sel(or_1_out));
  Multiplexer #(.width(7), .enable("false")) multiplexer_2 (
    .in0(7'b0000101), .in1(number_mapper_1_out_3), .out(multiplexer_2_out), .sel(or_2_out));
  Multiplexer #(.width(7), .enable("false")) multiplexer_3 (
    .in0(7'b0000101), .in1(number_mapper_1_out_4), .out(multiplexer_3_out), .sel(or_3_out));
  Multiplexer #(.width(7), .enable("false")) multiplexer_4 (
    .in0(7'b0000101), .in1(number_mapper_1_out_5), .out(multiplexer_4_out), .sel(decoder_1_out4));
  Multiplexer #(.width(7), .enable("false")) multiplexer_5 (
    .in0(multiplexer_1_out), .in1(alpha_mapper_1_out_2), .out(multiplexer_5_out), .sel(or_4_out));
  Multiplexer #(.width(7), .enable("false")) multiplexer_6 (
    .in0(multiplexer_2_out), .in1(alpha_mapper_1_out_3), .out(multiplexer_6_out), .sel(or_4_out));
  Multiplexer #(.width(7), .enable("false")) multiplexer_7 (
    .in0(multiplexer_3_out), .in1(alpha_mapper_1_out_4), .out(multiplexer_7_out), .sel(or_4_out));
  Multiplexer #(.width(7), .enable("false")) multiplexer_8 (
    .in0(multiplexer_4_out), .in1(alpha_mapper_1_out_5), .out(multiplexer_8_out), .sel(or_4_out));
  DotMatrix #(.matrixcols(23)) dotmatrix_1 (
    .col0(out_4), .col1(out_5), .col2(out_6), .col3(out_7), .col4(out_8), .col5({7{1'b0}}), .col6(out_10),
    .col7(out_11), .col8(out_12), .col9(out_13), .col10(out_14), .col11({7{1'b0}}), .col12(out_16),
    .col13(out_17), .col14(out_18), .col15(out_19), .col16(out_20), .col17({7{1'b0}}), .col18(out_22),
    .col19(out_23), .col20(out_24), .col21(out_25), .col22(out_26));
  Word_Mapper word_mapper_1 (
    .in_1(multiplexer_5_out), .out_2(out_4), .out_3(out_5), .out_4(out_6), .out_5(out_7), .out_6(out_8));
  Word_Mapper word_mapper_2 (
    .in_1(multiplexer_6_out), .out_2(out_10), .out_3(out_11), .out_4(out_12), .out_5(out_13), .out_6(out_14));
  Word_Mapper word_mapper_3 (
    .in_1(multiplexer_7_out), .out_2(out_16), .out_3(out_17), .out_4(out_18), .out_5(out_19), .out_6(out_20));
  Word_Mapper word_mapper_4 (
    .in_1(multiplexer_8_out), .out_2(out_22), .out_3(out_23), .out_4(out_24), .out_5(out_25), .out_6(out_26));

  assign out_9 = {7{1'b0}};
  assign out_15 = {7{1'b0}};
  assign out_21 = {7{1'b0}};

  // Notes on the sheet:
  //   第一层选择器
  //   决定显示数字或横杠
  //   显示器驱动
  //   第二层选择器
  //   决定显示数字或状态
endmodule

module Word_Mapper (
  input  [6:0] in_1,
  output [6:0] out_2,
  output [6:0] out_3,
  output [6:0] out_4,
  output [6:0] out_5,
  output [6:0] out_6
);

  wire [6:0] adder_1_out, adder_2_out, adder_3_out, adder_4_out, adder_5_out;

  Adder #(.width(7)) adder_1 (.a(in_1), .b({7{1'b0}}), .out(adder_1_out));  // open: cin, cout
  Adder #(.width(7)) adder_2 (.a(in_1), .b(7'b0000001), .out(adder_2_out));  // open: cin, cout
  Adder #(.width(7)) adder_3 (.a(in_1), .b(7'b0000010), .out(adder_3_out));  // open: cin, cout
  Adder #(.width(7)) adder_4 (.a(in_1), .b(7'b0000011), .out(adder_4_out));  // open: cin, cout
  Adder #(.width(7)) adder_5 (.a(in_1), .b(7'b0000100), .out(adder_5_out));  // open: cin, cout
  ROM #(.addrWidth(7), .dataWidth(7), .Select("low")) \u_字库  (.addr(adder_1_out), .data(out_2));
  ROM #(.addrWidth(7), .dataWidth(7), .Select("low")) rom_1 (.addr(adder_2_out), .data(out_3));
  ROM #(.addrWidth(7), .dataWidth(7), .Select("low")) rom_2 (.addr(adder_3_out), .data(out_4));
  ROM #(.addrWidth(7), .dataWidth(7), .Select("low")) rom_3 (.addr(adder_4_out), .data(out_5));
  ROM #(.addrWidth(7), .dataWidth(7), .Select("low")) rom_4 (.addr(adder_5_out), .data(out_6));

  // Notes on the sheet:
  //   传入字库中某个字的首地址 返回这个字的数据
  //   contents of 字库 (hex, n*v repeats v):
  //   6*0 8 8 8 0 3e 45 49 51 3e 0 21 7f 1 0 21 43 45 49 31 22 49 49 49 36 3f 48 48 48 3f 3e 41 41 41 22
  //   7f 49 49 49 41 7f 48 48 40 40 0 41 7f 41 0 7f 8 14 22 41 7f 4*1 7f 20 18 20 7f 7f 10 8 4 7f 3e 41 41
  //   41 3e 7f 48 48 48 30 0 0 7d 0 0 32 49 49 49 26 40 40 7f 40 40
  //   contents of rom_1 (hex, n*v repeats v):
  //   6*0 8 8 8 0 3e 45 49 51 3e 0 21 7f 1 0 21 43 45 49 31 22 49 49 49 36 3f 48 48 48 3f 3e 41 41 41 22
  //   7f 49 49 49 41 7f 48 48 40 40 0 41 7f 41 0 7f 8 14 22 41 7f 4*1 7f 20 18 20 7f 7f 10 8 4 7f 3e 41 41
  //   41 3e 7f 48 48 48 30 0 0 7d 0 0 32 49 49 49 26 40 40 7f 40 40
  //   contents of rom_2 (hex, n*v repeats v):
  //   6*0 8 8 8 0 3e 45 49 51 3e 0 21 7f 1 0 21 43 45 49 31 22 49 49 49 36 3f 48 48 48 3f 3e 41 41 41 22
  //   7f 49 49 49 41 7f 48 48 40 40 0 41 7f 41 0 7f 8 14 22 41 7f 4*1 7f 20 18 20 7f 7f 10 8 4 7f 3e 41 41
  //   41 3e 7f 48 48 48 30 0 0 7d 0 0 32 49 49 49 26 40 40 7f 40 40
  //   contents of rom_3 (hex, n*v repeats v):
  //   6*0 8 8 8 0 3e 45 49 51 3e 0 21 7f 1 0 21 43 45 49 31 22 49 49 49 36 3f 48 48 48 3f 3e 41 41 41 22
  //   7f 49 49 49 41 7f 48 48 40 40 0 41 7f 41 0 7f 8 14 22 41 7f 4*1 7f 20 18 20 7f 7f 10 8 4 7f 3e 41 41
  //   41 3e 7f 48 48 48 30 0 0 7d 0 0 32 49 49 49 26 40 40 7f 40 40
  //   contents of rom_4 (hex, n*v repeats v):
  //   6*0 8 8 8 0 3e 45 49 51 3e 0 21 7f 1 0 21 43 45 49 31 22 49 49 49 36 3f 48 48 48 3f 3e 41 41 41 22
  //   7f 49 49 49 41 7f 48 48 40 40 0 41 7f 41 0 7f 8 14 22 41 7f 4*1 7f 20 18 20 7f 7f 10 8 4 7f 3e 41 41
  //   41 3e 7f 48 48 48 30 0 0 7d 0 0 32 49 49 49 26 40 40 7f 40 40
endmodule

module Alpha_Mapper (
  input  [2:0] Condition,
  output [6:0] out_2,
  output [6:0] out_3,
  output [6:0] out_4,
  output [6:0] out_5
);

  wire [4:0] adder_1_out, adder_2_out, adder_3_out, adder_4_out, multiplexer_1_out;

  Multiplexer #(.select(3), .width(5), .enable("false")) multiplexer_1 (
    .in0(5'b10100), .in1({5{1'b0}}), .in2(5'b00100), .in3(5'b01000), .in4(5'b01100), .in5(5'b10000),
    .out(multiplexer_1_out), .sel(Condition));  // open: in6, in7
  Adder #(.width(5)) adder_1 (.a(multiplexer_1_out), .b({5{1'b0}}), .out(adder_1_out));  // open: cin, cout
  Adder #(.width(5)) adder_2 (.a(multiplexer_1_out), .b(5'b00001), .out(adder_2_out));  // open: cin, cout
  Adder #(.width(5)) adder_3 (.a(multiplexer_1_out), .b(5'b00010), .out(adder_3_out));  // open: cin, cout
  Adder #(.width(5)) adder_4 (.a(multiplexer_1_out), .b(5'b00011), .out(adder_4_out));  // open: cin, cout
  ROM #(.addrWidth(5), .dataWidth(7), .Select("low")) \u_词库  (.addr(adder_1_out), .data(out_2));
  ROM #(.addrWidth(5), .dataWidth(7), .Select("low")) rom_1 (.addr(adder_2_out), .data(out_3));
  ROM #(.addrWidth(5), .dataWidth(7), .Select("low")) rom_2 (.addr(adder_3_out), .data(out_4));
  ROM #(.addrWidth(5), .dataWidth(7), .Select("low")) rom_3 (.addr(adder_4_out), .data(out_5));

  // Notes on the sheet:
  //   把状态编号先映射到首地址
  //   转化为四个字的首地址
  //   contents of 词库 (hex, n*v repeats v):
  //   2d 1e 32 3c 4b 50 28 46 5a 28 5f 55 5f 32 41 28 3c 4b 23 37
  //   contents of rom_1 (hex, n*v repeats v):
  //   2d 1e 32 3c 4b 50 28 46 5a 28 5f 55 5f 32 41 28 3c 4b 23 37
  //   contents of rom_2 (hex, n*v repeats v):
  //   2d 1e 32 3c 4b 50 28 46 5a 28 5f 55 5f 32 41 28 3c 4b 23 37
  //   contents of rom_3 (hex, n*v repeats v):
  //   2d 1e 32 3c 4b 50 28 46 5a 28 5f 55 5f 32 41 28 3c 4b 23 37
endmodule

module Number_Mapper (
  input  [7:0] Input,
  output [6:0] out_2,
  output [6:0] out_3,
  output [6:0] out_4,
  output [6:0] out_5
);

  Multiplexer #(.select(2), .width(7), .enable("false")) multiplexer_1 (
    .in0(7'b0001010), .in1(7'b0001111), .in2(7'b0010100), .in3(7'b0011001), .out(out_2), .sel(Input[1:0]));
  Multiplexer #(.select(2), .width(7), .enable("false")) multiplexer_2 (
    .in0(7'b0001010), .in1(7'b0001111), .in2(7'b0010100), .in3(7'b0011001), .out(out_3), .sel(Input[3:2]));
  Multiplexer #(.select(2), .width(7), .enable("false")) multiplexer_3 (
    .in0(7'b0001010), .in1(7'b0001111), .in2(7'b0010100), .in3(7'b0011001), .out(out_4), .sel(Input[5:4]));
  Multiplexer #(.select(2), .width(7), .enable("false")) multiplexer_4 (
    .in0(7'b0001010), .in1(7'b0001111), .in2(7'b0010100), .in3(7'b0011001), .out(out_5), .sel(Input[7:6]));

  // Notes on the sheet:
  //   这里的 0a of 14 19 分别是字库中 0 1 2 3 4 的首地址
endmodule

module Timer_Locker (
  input  [2:0] Input_Count,
  input  Clock,
  input  Timer_Reset,
  output Time_Out
);

  wire counter_1_carry, not_1_out, or_1_out, or_2_out;

  or or_1 (or_1_out, Input_Count[0], Input_Count[1], Input_Count[2]);
  not not_1 (not_1_out, or_1_out);
  Counter #(.width(10), .max('h1f4)) counter_1 (
    .count(or_1_out), .carry(counter_1_carry), .clk(Clock), .clr(or_2_out));  // open: load, D, Q, preset, down
  or or_2 (or_2_out, not_1_out, Timer_Reset);
  Delay_Timer delay_timer_1 (.Times(10'h64), .Signal(counter_1_carry), .Delay_Signal(Time_Out), .Clock(Clock));

  // Notes on the sheet:
  //   超时报错
  //   超时进位
  //   延迟显示
endmodule

module Times_Locker (
  input  Fail,
  input  Clock,
  input  Reset,
  output Time_Out
);

  wire counter_1_carry, or_1_out;

  Counter #(.width(2), .max('h3)) counter_1 (
    .carry(counter_1_carry), .clk(Fail), .clr(or_1_out));  // open: load, D, count, Q, preset, down
  or or_1 (or_1_out, Reset, Time_Out);
  Delay_Timer delay_timer_1 (.Times(10'h1f4), .Signal(counter_1_carry), .Delay_Signal(Time_Out), .Clock(Clock));

  // Notes on the sheet:
  //   次数报错
  //   计数进位
  //   延迟显示
endmodule

module Processor (
  input  Result,
  input  [2:0] Count,
  input  Enter,
  input  Set,
  input  Timer_out,
  input  Times_Out,
  input  Reset,
  input  Clock,
  output Fail,
  output Flash_Out,
  output Timer_Reset,
  output Times_Reset,
  output [2:0] Condition,
  output Clean
);

  wire and_1_out, delay_timer_1_delay_signal, delay_timer_2_delay_signal, delay_timer_3_delay_signal,
       delay_timer_4_delay_signal, failling_edge_1_failling_edge, flashing_led_1_flash_out, not_1_out,
       not_2_out;
  wire [2:0] multiplexer_1_out, multiplexer_2_out, multiplexer_4_out, multiplexer_5_out;

  and and_1 (and_1_out, Result, Count[2]);
  and and_2 (Fail, Enter, not_1_out);
  not not_1 (not_1_out, and_1_out);
  and and_3 (Times_Reset, and_1_out, Enter);
  Delay_Timer delay_timer_1 (.Times(10'hc8), .Signal(Set), .Delay_Signal(delay_timer_1_delay_signal), .Clock(Clock));
  Failling_Edge failling_edge_1 (
    .Input(delay_timer_4_delay_signal), .Clock(Clock), .Failling_Edge(failling_edge_1_failling_edge));
  Delay_Timer delay_timer_2 (.Times(10'hc8), .Signal(Fail), .Delay_Signal(delay_timer_2_delay_signal), .Clock(Clock));
  Delay_Timer delay_timer_3 (.Times(10'hc8), .Signal(Enter), .Delay_Signal(delay_timer_3_delay_signal), .Clock(Clock));
  Delay_Timer delay_timer_4 (
    .Times(10'hc8), .Signal(Times_Reset), .Delay_Signal(delay_timer_4_delay_signal), .Clock(Clock));
  Multiplexer #(.width(3), .enable("false")) multiplexer_1 (
    .in0(3'b001), .in1(3'b010), .out(multiplexer_1_out), .sel(delay_timer_4_delay_signal));
  not not_2 (not_2_out, delay_timer_2_delay_signal);
  Flashing_LED flashing_led_1 (
    .Enable(delay_timer_2_delay_signal), .Clock(Clock), .Flash_Out(flashing_led_1_flash_out));
  Multiplexer #(.width(3), .enable("false")) multiplexer_2 (
    .in0(3'b000), .in1(multiplexer_1_out), .out(multiplexer_2_out), .sel(delay_timer_3_delay_signal));
  or or_1 (Clean, failling_edge_1_failling_edge, Timer_out, Times_Out, Reset, Fail);
  Multiplexer #(.enable("false")) multiplexer_3 (
    .in0(flashing_led_1_flash_out), .in1(delay_timer_4_delay_signal), .out(Flash_Out), .sel(not_2_out));
  Multiplexer #(.width(3), .enable("false")) multiplexer_4 (
    .in0(multiplexer_2_out), .in1(3'b011), .out(multiplexer_4_out), .sel(delay_timer_1_delay_signal));
  Multiplexer #(.width(3), .enable("false")) multiplexer_5 (
    .in0(multiplexer_4_out), .in1(3'b100), .out(multiplexer_5_out), .sel(Timer_out));
  Multiplexer #(.width(3), .enable("false")) multiplexer_6 (
    .in0(multiplexer_5_out), .in1(3'b101), .out(Condition), .sel(Times_Out));

  assign Timer_Reset = Enter;

  // Notes on the sheet:
  //   判断正确逻辑
  //   Enter重置时钟
  //   正确重置次数
  //   状态处理机
  //   多种情况引发重置输入
  //   Delay均为延迟显示
endmodule

module Failling_Edge (
  input  Input,
  input  Clock,
  output Failling_Edge
);

  wire register_1_q, register_2_q;

  Register #(.width(1), .Select("low")) register_1 (.D(Input), .Q(register_1_q), .clk(Clock));  // open: en, clr
  Register #(.width(1), .Select("low")) register_2 (.D(register_1_q), .Q(register_2_q), .clk(Clock));  // open: en, clr
  and and_1 (Failling_Edge, ~register_1_q, register_2_q);  // AND_Gate

  // Notes on the sheet:
  //   下降沿捕获器
endmodule

module Delay_Timer (
  input  [9:0] Times,
  input  Signal,
  input  Clock,
  output Delay_Signal
);

  wire counter_1_carry, or_1_out;

  or or_1 (or_1_out, Signal, Delay_Signal);
  Counter #(.width(10), .max('h3ff)) counter_1 (
    .load(Signal), .D(Times), .count(or_1_out), .carry(counter_1_carry), .clk(Clock), .down(1'b1));  // open: Q, clr, preset
  S_R_Flip_Flop s_r_ff_1 (.S(Signal), .clk(Clock), .R(counter_1_carry), .Q(Delay_Signal));  // open: Qn, preset, reset

  // Notes on the sheet:
  //   信号延迟器
endmodule

module Flashing_LED (
  input  Enable,
  input  Clock,
  output Flash_Out
);

  wire counter_1_carry;

  Counter #(.max('h32)) counter_1 (
    .count(Enable), .carry(counter_1_carry), .clk(Clock));  // open: load, D, Q, clr, preset, down
  Delay_Timer delay_timer_1 (.Times(10'h19), .Signal(counter_1_carry), .Delay_Signal(Flash_Out), .Clock(Clock));

  // Notes on the sheet:
  //   n个周期产生进位信号
  //   LED 闪烁发生器
  //   捕获下降沿并延时n/2个周期
endmodule

module TOP (
);

  wire _0_out, _1_out, _2_out, _3_out, C_out, E_out, main_1_out_32, main_1_out_33;
  wire [6:0] main_1_flash, main_1_flash_2, main_1_out_7, main_1_out_8, main_1_out_9, main_1_out_10,
       main_1_out_11, main_1_out_12, main_1_out_13, main_1_out_14, main_1_out_15, main_1_out_16,
       main_1_out_17, main_1_out_18, main_1_out_19, main_1_out_20, main_1_out_21, main_1_out_22,
       main_1_out_23, main_1_out_24, main_1_out_25, main_1_out_26, main_1_out_27, main_1_out_28,
       main_1_out_29, main_1_out_34, main_1_out_35;

  DotMatrix #(.matrixcols(27)) dotmatrix_1 (
    .col0(main_1_flash_2), .col1(main_1_out_34), .col2(main_1_out_7), .col3(main_1_out_8),
    .col4(main_1_out_9), .col5(main_1_out_10), .col6(main_1_out_11), .col7(main_1_out_12),
    .col8(main_1_out_13), .col9(main_1_out_14), .col10(main_1_out_15), .col11(main_1_out_16),
    .col12(main_1_out_17), .col13(main_1_out_18), .col14(main_1_out_19), .col15(main_1_out_20),
    .col16(main_1_out_21), .col17(main_1_out_22), .col18(main_1_out_23), .col19(main_1_out_24),
    .col20(main_1_out_25), .col21(main_1_out_26), .col22(main_1_out_27), .col23(main_1_out_28),
    .col24(main_1_out_29), .col25(main_1_out_35), .col26(main_1_flash));
  Button E (.out(E_out));
  Button C (.out(C_out));
  Button _0 (.out(_0_out));
  Button _3 (.out(_3_out));
  Button _1 (.out(_1_out));
  Button _2 (.out(_2_out));
  main main_1 (
    .out_7(main_1_out_7), .out_8(main_1_out_8), .out_9(main_1_out_9), .out_10(main_1_out_10),
    .out_11(main_1_out_11), .out_12(main_1_out_12), .out_13(main_1_out_13), .out_14(main_1_out_14),
    .out_15(main_1_out_15), .out_16(main_1_out_16), .out_17(main_1_out_17), .out_18(main_1_out_18),
    .out_19(main_1_out_19), .out_20(main_1_out_20), .out_21(main_1_out_21), .out_22(main_1_out_22),
    .out_23(main_1_out_23), .out_24(main_1_out_24), .out_25(main_1_out_25), .out_26(main_1_out_26),
    .out_27(main_1_out_27), .out_28(main_1_out_28), .out_29(main_1_out_29), .Reset(C_out), .Enter(E_out),
    .P0(_0_out), .P1(_1_out), .P2(_2_out), .P3(_3_out), .Flash(main_1_flash), .Flash_2(main_1_flash_2),
    .out_35(main_1_out_35), .out_34(main_1_out_34), .out_32(main_1_out_32), .out_33(main_1_out_33));

  // Notes on the sheet:
  //   C i a l l o～(∠·ω< )⌒☆
endmodule

module Flow_Flash (
  input  Enable,
  input  Clock,
  output [6:0] Flash_Out_0,
  output [6:0] Flash_Out_1
);

  wire and_1_out, clock_1_out, failling_edge_1_failling_edge, failling_edge_2_failling_edge,
       failling_edge_3_failling_edge, failling_edge_4_failling_edge, failling_edge_5_failling_edge,
       failling_edge_6_failling_edge, failling_edge_7_failling_edge, failling_edge_8_failling_edge,
       failling_edge_9_failling_edge, failling_edge_10_failling_edge, failling_edge_11_failling_edge,
       failling_edge_12_failling_edge, failling_edge_13_failling_edge, failling_edge_14_failling_edge,
       or_1_out, or_2_out, register_1_q, register_2_q;

  DotMatrix #(.matrixcols(2)) dotmatrix_1 (.col0(Flash_Out_0), .col1(Flash_Out_1));
  Clock clock_1 (.out(clock_1_out));
  Register #(.width(1), .Select("low")) register_1 (.D(Enable), .Q(register_1_q), .clk(clock_1_out));  // open: en, clr
  or or_1 (or_1_out, register_1_q, failling_edge_2_failling_edge);
  Register #(.width(1), .Select("low")) register_2 (
    .D(register_1_q), .Q(register_2_q), .clk(clock_1_out));  // open: en, clr
  and and_1 (and_1_out, or_1_out, ~register_2_q);  // AND_Gate
  Delay_Timer delay_timer_1 (.Times(10'hc), .Signal(and_1_out), .Delay_Signal(Flash_Out_0[0]), .Clock(clock_1_out));
  Failling_Edge failling_edge_1 (
    .Input(Flash_Out_0[0]), .Clock(clock_1_out), .Failling_Edge(failling_edge_1_failling_edge));
  Delay_Timer delay_timer_2 (
    .Times(10'hc), .Signal(failling_edge_1_failling_edge), .Delay_Signal(Flash_Out_0[1]), .Clock(clock_1_out));
  Failling_Edge failling_edge_2 (.Input(or_2_out), .Clock(clock_1_out), .Failling_Edge(failling_edge_2_failling_edge));
  Failling_Edge failling_edge_3 (
    .Input(Flash_Out_0[1]), .Clock(clock_1_out), .Failling_Edge(failling_edge_3_failling_edge));
  Delay_Timer delay_timer_3 (
    .Times(10'hc), .Signal(failling_edge_3_failling_edge), .Delay_Signal(Flash_Out_0[2]), .Clock(clock_1_out));
  Failling_Edge failling_edge_4 (
    .Input(Flash_Out_0[2]), .Clock(clock_1_out), .Failling_Edge(failling_edge_4_failling_edge));
  Delay_Timer delay_timer_4 (
    .Times(10'hc), .Signal(failling_edge_4_failling_edge), .Delay_Signal(Flash_Out_0[3]), .Clock(clock_1_out));
  Failling_Edge failling_edge_5 (
    .Input(Flash_Out_0[3]), .Clock(clock_1_out), .Failling_Edge(failling_edge_5_failling_edge));
  Delay_Timer delay_timer_5 (
    .Times(10'hc), .Signal(failling_edge_5_failling_edge), .Delay_Signal(Flash_Out_0[4]), .Clock(clock_1_out));
  Failling_Edge failling_edge_6 (
    .Input(Flash_Out_0[4]), .Clock(clock_1_out), .Failling_Edge(failling_edge_6_failling_edge));
  Delay_Timer delay_timer_6 (
    .Times(10'hc), .Signal(failling_edge_6_failling_edge), .Delay_Signal(Flash_Out_0[5]), .Clock(clock_1_out));
  Failling_Edge failling_edge_7 (
    .Input(Flash_Out_0[5]), .Clock(clock_1_out), .Failling_Edge(failling_edge_7_failling_edge));
  Delay_Timer delay_timer_7 (
    .Times(10'hc), .Signal(failling_edge_7_failling_edge), .Delay_Signal(Flash_Out_0[6]), .Clock(clock_1_out));
  Failling_Edge failling_edge_8 (
    .Input(Flash_Out_0[6]), .Clock(clock_1_out), .Failling_Edge(failling_edge_8_failling_edge));
  or or_2 (or_2_out, Flash_Out_1[6], Flash_Out_1[0]);
  Delay_Timer delay_timer_8 (
    .Times(10'hc), .Signal(failling_edge_8_failling_edge), .Delay_Signal(Flash_Out_1[6]), .Clock(clock_1_out));
  Failling_Edge failling_edge_9 (
    .Input(Flash_Out_1[6]), .Clock(clock_1_out), .Failling_Edge(failling_edge_9_failling_edge));
  Delay_Timer delay_timer_9 (
    .Times(10'hc), .Signal(failling_edge_9_failling_edge), .Delay_Signal(Flash_Out_1[5]), .Clock(clock_1_out));
  Failling_Edge failling_edge_10 (
    .Input(Flash_Out_1[5]), .Clock(clock_1_out), .Failling_Edge(failling_edge_10_failling_edge));
  Delay_Timer delay_timer_10 (
    .Times(10'hc), .Signal(failling_edge_10_failling_edge), .Delay_Signal(Flash_Out_1[4]), .Clock(clock_1_out));
  Failling_Edge failling_edge_11 (
    .Input(Flash_Out_1[4]), .Clock(clock_1_out), .Failling_Edge(failling_edge_11_failling_edge));
  Delay_Timer delay_timer_11 (
    .Times(10'hc), .Signal(failling_edge_11_failling_edge), .Delay_Signal(Flash_Out_1[3]), .Clock(clock_1_out));
  Failling_Edge failling_edge_12 (
    .Input(Flash_Out_1[3]), .Clock(clock_1_out), .Failling_Edge(failling_edge_12_failling_edge));
  Failling_Edge failling_edge_13 (
    .Input(Flash_Out_1[2]), .Clock(clock_1_out), .Failling_Edge(failling_edge_13_failling_edge));
  Delay_Timer delay_timer_12 (
    .Times(10'hc), .Signal(failling_edge_12_failling_edge), .Delay_Signal(Flash_Out_1[2]), .Clock(clock_1_out));
  Delay_Timer delay_timer_13 (
    .Times(10'hc), .Signal(failling_edge_13_failling_edge), .Delay_Signal(Flash_Out_1[1]), .Clock(clock_1_out));
  Failling_Edge failling_edge_14 (
    .Input(Flash_Out_1[1]), .Clock(clock_1_out), .Failling_Edge(failling_edge_14_failling_edge));
  Delay_Timer delay_timer_14 (
    .Times(10'hc), .Signal(failling_edge_14_failling_edge), .Delay_Signal(Flash_Out_1[0]), .Clock(clock_1_out));

  // Notes on the sheet:
  //   一个小彩蛋~
  //   重复开关几次enable，然后再开关一次enable就可以实现流水效果，最后变成闪灯
endmodule
